# Fritzing sketch chickencoopdoor_esp8266 (saved by Fritzing 0.9.4)
breadboards: 1

parts:
  Tiny_RTC = Real Time Clock Module - DS1307 RTC Breakout Board
  WeMos_D1_Mini1 = WeMos D1 Mini

nets:
  5V: Tiny_RTC.5V, WeMos_D1_Mini1.5V
  N1: Tiny_RTC.GND, WeMos_D1_Mini1.G
  N2: Tiny_RTC.SCL, WeMos_D1_Mini1.D1
  N3: Tiny_RTC.SDA, WeMos_D1_Mini1.D2
